# Fritzing sketch connnection_diagram_esp32-rotary-encoder-NG (saved by Fritzing 0.9.4)

parts:
  MH-ET_LIVE_ESP32_DEVKIT1 = MH-ET LIVE ESP32 DEVKIT 38 pins
  RE1 = Rotary Encoder [package=THT]

nets:
  N1: MH-ET_LIVE_ESP32_DEVKIT1.IO32, RE1.EncoderPinA
  N2: MH-ET_LIVE_ESP32_DEVKIT1.IO25, RE1.EncoderPinB
  N3: MH-ET_LIVE_ESP32_DEVKIT1.IO26, RE1.SwitchrPinD
  N4: MH-ET_LIVE_ESP32_DEVKIT1.GND, RE1.EncoderPinC, RE1.SwitchPinE

custom parts:
  MH-ET LIVE ESP32 DEVKIT 38 pins: http://mh.nodebb.com/topic/2/mh-et-live-esp32-devkit
  Rotary Encoder: Rotary Encoder from ALPSec11e with switch. This version has an alternate (which has been used in boards) pcb footprint from @opera_night in the forums. It is probably the best one to start from to see if you part matches.
